# Fritzing sketch Simple LED (saved by Fritzing 0.9.2b)
breadboards: 1

parts:
  Raspberry_Pi1 = Raspberry Pi 2
  R1 = Resistor [tolerance=±5% resistance=220 package="1206 [SMD]"]
  LED1 = LED - 3mm [color="Red (633nm)" package="3 mm [THT]"]

nets:
  N1: Raspberry_Pi1.GPIO4, R1.Pin_0
  N2: Raspberry_Pi1.GND, LED1.anode
  N3: R1.Pin_1, LED1.cathode
